# Fritzing sketch Weighted 4 (saved by Fritzing 0.8.7b)
breadboards: 1

parts:
  Eleman1 = Arduino Uno (Rev3)
  Eleman2 = Bluetooth HC-05 Macho
  U1 = ESP8266 WiFi Module [part_number=ESP8266]
  S1 = Load Sensor - 50kg [part_number=SEN-10245]
  R1 = Resistor [tolerance=±5% resistance=220 package=THT]
  R2 = Resistor [tolerance=±5% resistance=220 package=THT]
  Eleman3 = HX711 Weighing Sensor Module

nets:
  N1: Eleman1.D8, Eleman2.State
  N2: Eleman1.D9_PWM, Eleman2.RXD
  N3: Eleman1.D10_PWM/SS, Eleman2.TXD
  GND: Eleman1.GND, Eleman2.GND, U1.GND, Eleman3.GND
  N4: Eleman1.D2, Eleman3.CK/TX
  N5: Eleman1.D3_PWM, Eleman3.DO/RX
  N6: Eleman1.D4, U1.TXD
  N7: Eleman1.D5_PWM, U1.RXD
  3V3: Eleman1.3V3, U1.VCC, U1.CH_PD
  VCC: Eleman1.5V, Eleman2.VCC, Eleman3.VCC
  N8: S1.B, R2.Pin_1, Eleman3.E-
  N9: S1.W, R1.Pin_1, Eleman3.E+
  N10: S1.R, Eleman3.A+
  N11: R1.Pin_0, R2.Pin_0, Eleman3.A-

custom parts:
  ESP8266 WiFi Module: Generic WiFi Module based on the ESP8266 with onboard PCB antenna and UART communications
  Load Sensor - 50kg: Half-wheatstone bridge Load Cell modified from the Fritzing Repo This load sensor, sometimes called a strain gauge, is the same one found in digital bathroom scales (you know, the ones you use in January for your New Year's resolutions, and then forget about a month later). This sensor can measure up to about 110 pounds.
